# Fritzing sketch project (saved by Fritzing 0.9.4)
breadboards: 1

parts:
  IC1 = MICROCONTROLLER [package=dil28-3-simon-kit]
  S1 = Pushbutton [package="[THT]"]
  S2 = Pushbutton [package="[THT]"]
  S3 = Pushbutton [package="[THT]"]
  S4 = Pushbutton [package="[THT]"]
  S5 = Pushbutton [package="[THT]"]
  LED2 = LED - 5mm [color="Blue (430nm)" package="5 mm [THT]"]
  LED3 = LED - 5mm [color="Green (560nm)" package="5 mm [THT]"]
  LED4 = LED - 5mm [color="Yellow (595nm)" package="5 mm [THT]"]
  R1 = Resistor [tolerance=±5% resistance=10k package=THT]
  R2 = Resistor [tolerance=±5% resistance=10k package=THT]
  R3 = Resistor [tolerance=±5% resistance=10k package=THT]
  R4 = Resistor [tolerance=±5% resistance=10k package=THT]
  R5 = Resistor [tolerance=±5% resistance=10k package=THT]
  R6 = Resistor [tolerance=±5% resistance=10k package=THT]
  R7 = Resistor [tolerance=±5% resistance=10k package=THT]
  R8 = Resistor [tolerance=±5% resistance=1k package=THT]
  R9 = Resistor [tolerance=±5% resistance=1k package=THT]
  R10 = Resistor [tolerance=±5% resistance=1k package=THT]
  R11 = Resistor [tolerance=±5% resistance=1k package=THT]
  R12 = Resistor [tolerance=±5% resistance=10k package=THT]
  R13 = Resistor [tolerance=±5% resistance=10k package=THT]
  Q1 = MOSFET-NCHANNEL [package=to-92]
  Q2 = MOSFET-NCHANNEL [package=to-92]
  Q3 = MOSFET-NCHANNEL [package=to-92]
  U1 = AVR 10-pin ICSP Header [package="avr icsp"]
  R14 = Resistor [tolerance=±5% resistance=100 package=THT]
  R15 = Resistor [tolerance=±5% resistance=100 package=THT]
  R16 = Resistor [tolerance=±5% resistance=100 package=THT]
  R17 = Resistor [tolerance=±5% resistance=1k package=THT]
  R18 = Resistor [tolerance=±5% resistance=1k package=THT]
  LED6 = LED - 5mm [color="Infrared (940nm)" package="5 mm [THT]"]
  Q4 = npn-Powertransistor [package="TO220 [THT]"]
  Q5 = NPN-Transistor [package="TO92 [THT]"]
  M1 = DC Motor
  LED1 = smd LED [color="Red (633nm)" package="1206 [SMD]"]
  LED5 = smd LED [color="Red (633nm)" package="1206 [SMD]"]
  Part1 = IR Receiver Breakout [package=PCB]
  J1 = ATX24 Pin Power Supply Connector [package=atx24_right_angle]
  D1 = Rectifier Diode 10A [part_number=P1000K]
  M2 = DC Motor

nets:
  N1: IC1.PC6(_RESET), U1.5
  N2: IC1.PD0(RXD), S5.Pin_1, S5.Pin_2, R7.Pin_1
  N3: IC1.PD1(TXD), S1.Pin_1, S1.Pin_2, R3.Pin_1
  N4: IC1.PD2(INT0), R12.Pin_0, Part1.GND
  N5: IC1.PD3(INT1), R13.Pin_0
  N6: IC1.PD4(XCK_T0), LED1.anode
  N7: IC1.VCC, S1.Pin_3, S1.Pin_4, S2.Pin_3, S2.Pin_4, S3.Pin_3, S3.Pin_4, S4.Pin_3, S4.Pin_4, S5.Pin_3, S5.Pin_4, R2.Pin_0, Q2.S, U1.2
  GND: IC1.GND, IC1.AGND, R1.Pin_0, R3.Pin_0, R4.Pin_0, R5.Pin_0, R6.Pin_0, R7.Pin_0, R8.Pin_1, R9.Pin_1, R10.Pin_1, R11.Pin_1, R12.Pin_1, R13.Pin_1, Q1.D, Q3.D, U1.6, LED6.cathode, Q4.emitter, J1.GND, M2.pin_1
  N8: IC1.PB6(XTAL1_TOSC1), S2.Pin_1, S2.Pin_2, R4.Pin_1
  N9: IC1.PB7(XTAL2_TOSC2), LED4.anode
  N10: IC1.PD5(T1), LED2.anode
  N11: IC1.PD6(AIN0), S4.Pin_1, S4.Pin_2, R6.Pin_1
  N12: IC1.PD7(AIN1), S3.Pin_1, S3.Pin_2, R5.Pin_1
  N13: IC1.PB0(ICP), LED3.anode
  N14: IC1.PB1(OC1A), R16.Pin_1
  N15: IC1.PB3(MOSI_OC2), U1.1
  N16: IC1.PB4(MISO), U1.9
  N17: IC1.PB5(SCK), U1.7
  N18: IC1.PC2(ADC2), R1.Pin_1, Q2.D
  N19: IC1.PC4(ADC4_SDA), Q3.G
  N20: IC1.PC5(ADC5_SCL), Q1.G
  N21: LED2.cathode, R9.Pin_0
  N22: LED3.cathode, R10.Pin_0
  N23: LED4.cathode, R8.Pin_0
  N24: R2.Pin_1, Part1.VCC
  N25: R11.Pin_0, LED1.cathode
  N26: Q1.S, Q2.G, J1.PS_ON
  N27: Q3.S, LED5.cathode
  N28: R14.Pin_0, R15.Pin_0, Q5.C
  N29: R14.Pin_1, R15.Pin_1, J1.3.3V
  N30: R16.Pin_0, Q5.B
  N31: R17.Pin_0, R18.Pin_0, LED6.anode
  N32: R17.Pin_1, R18.Pin_1, M1.pin_2, LED5.anode, J1.5V, D1.cathode
  N33: Q4.base, Q5.E
  N34: Q4.collector, M1.pin_1, D1.anode
  N35: J1.12V, M2.pin_2

notes:
  1
  2
  3
  4
  5
  6
  7
  8
  9
  10
  11
  12
  13
  14
